// Logisim project 1607003_ALU_Arithmetic_logic.circ as structural Verilog: 5 circuits, main circuit ALU
module ALU (
  input  S2,
  input  S1,
  input  S0,
  input  Cin,
  input  A0,
  input  B0,
  input  A1,
  input  B1,
  input  A2,
  input  B2,
  input  A3,
  input  B3,
  output F0,
  output F1,
  output F2,
  output F3,
  output Cout
);

  wire and_1_out, and_2_out, and_3_out, and_4_out, complementor_1_b_or_b_com, complementor_2_b_or_b_com,
       complementor_3_b_or_b_com, complementor_4_b_or_b_com, extension_1_xi, extension_2_xi, extension_3_xi,
       extension_4_xi, full_adder_1_c_out, full_adder_2_c_out, full_adder_3_c_out, not_1_out, not_2_out,
       not_3_out, not_4_out;

  not not_1 (not_1_out, S2);
  not not_2 (not_2_out, S2);
  not not_3 (not_3_out, S2);
  not not_4 (not_4_out, S2);
  and and_1 (and_1_out, not_4_out, Cin);
  extension extension_1 (.A(A0), .S0(S0), .S1(S1), .S2(S2), .B(B0), .Xi(extension_1_xi));
  complementor complementor_1 (.B(B0), .S0(S0), .S1(S1), .B_Or_B_Com(complementor_1_b_or_b_com));
  and and_2 (and_2_out, full_adder_1_c_out, not_1_out);
  extension extension_2 (.A(A1), .S0(S0), .S1(S1), .S2(S2), .B(B1), .Xi(extension_2_xi));
  complementor complementor_2 (.B(B1), .S0(S0), .S1(S1), .B_Or_B_Com(complementor_2_b_or_b_com));
  and and_3 (and_3_out, full_adder_2_c_out, not_2_out);
  extension extension_3 (.A(A2), .S0(S0), .S1(S1), .S2(S2), .B(B2), .Xi(extension_3_xi));
  complementor complementor_3 (.B(B2), .S0(S0), .S1(S1), .B_Or_B_Com(complementor_3_b_or_b_com));
  and and_4 (and_4_out, full_adder_3_c_out, not_3_out);
  extension extension_4 (.A(A3), .S0(S0), .S1(S1), .S2(S2), .B(B3), .Xi(extension_4_xi));
  complementor complementor_4 (.B(B3), .S0(S0), .S1(S1), .B_Or_B_Com(complementor_4_b_or_b_com));
  Full_Adder full_adder_1 (
    .Cin(and_1_out), .A(extension_1_xi), .B(complementor_1_b_or_b_com), .Sum(F0), .C_Out(full_adder_1_c_out));
  Full_Adder full_adder_2 (
    .Cin(and_2_out), .A(extension_2_xi), .B(complementor_2_b_or_b_com), .Sum(F1), .C_Out(full_adder_2_c_out));
  Full_Adder full_adder_3 (
    .Cin(and_3_out), .A(extension_3_xi), .B(complementor_3_b_or_b_com), .Sum(F2), .C_Out(full_adder_3_c_out));
  Full_Adder full_adder_4 (.Cin(and_4_out), .A(extension_4_xi), .B(complementor_4_b_or_b_com), .Sum(F3), .C_Out(Cout));

  // Notes on the sheet:
  //   Extension for A
  //   Complementor
  //   Extension for A
  //   Complementor
  //   Extension for A
  //   Complementor
  //   Extension for A
  //   Complementor
  //   S' AND Cin
  //   S' AND Cin
  //   S' AND Cin
  //   S' AND Cin
  //   Full Adder
  //   Full Adder
  //   Full Adder
  //   Full Adder
  //   Here,
  //   A = 0011
  //   B = 0001
  //   Roll: 1607003
  //   Function 12,
  //   Name: Md Saiful Islam
  //   Complement A:         F = A'
endmodule

module Full_Adder (
  input  Cin,
  input  A,
  input  B,
  output Sum,
  output C_Out
);

  wire and_1_out, and_2_out, xor_1_out;

  xor xor_1 (xor_1_out, A, B);
  and and_1 (and_1_out, B, A);
  xor xor_2 (Sum, xor_1_out, Cin);
  and and_2 (and_2_out, Cin, xor_1_out);
  or or_1 (C_Out, and_2_out, and_1_out);

  // Notes on the sheet:
  //   Roll: 1607003
  //   Name: Md Saiful Islam
  //   A x-or B
  //   AB
  //   Cin ( A X-or B)
  //   = 
  //   Cin X-or ( A x-or B)
endmodule

module complementor (
  input  B,
  input  S0,
  input  S1,
  output B_Or_B_Com
);

  wire and_1_out, and_2_out, not_1_out;

  not not_1 (not_1_out, B);
  and and_1 (and_1_out, B, S0);
  and and_2 (and_2_out, not_1_out, S1);
  or or_1 (B_Or_B_Com, and_1_out, and_2_out);

  // Notes on the sheet:
  //   Name: Md Saiful Islam
  //   Roll: 1607003
endmodule

module extension (
  input  A,
  input  S0,
  input  S1,
  input  S2,
  input  B,
  output Xi
);

  wire and_1_out, and_2_out, not_1_out, not_2_out, not_3_out;

  not not_1 (not_1_out, B);
  not not_2 (not_2_out, S0);
  not not_3 (not_3_out, S1);
  and and_1 (and_1_out, S2, not_3_out, not_2_out, B);
  and and_2 (and_2_out, not_1_out, not_2_out, S1, S2);
  or or_1 (Xi, A, and_1_out, and_2_out);

  // Notes on the sheet:
  //   Name: Md Saiful Islam
  //   Roll: 1607003
endmodule

module ALU_IC (
);

  ALU alu_1 ();  // open: Cin, A0, B0, A1, B1, A2, B2, A3, B3, F0, F1, F2, F3, Cout, S2, S1, S0
endmodule
