// Logisim project 1607003_RTL.circ as structural Verilog: 3 circuits, main circuit main
module main (
  input  [3:0] Input,
  input  Reset,
  input  Enable,
  input  Load,
  input  Load_2,
  input  Enable_2,
  input  Reset_2,
  input  Reset_3,
  input  Enable_3,
  input  Load_3,
  input  Load_4,
  input  Enable_4,
  input  Reset_4,
  output [3:0] out_14
);

  Register register_1 (
    .load(Load), .X3(out_14[3]), .X2(out_14[2]), .X1(out_14[1]), .X0(out_14[0]), .Y3(out_14[3]),
    .Y2(out_14[2]), .Y1(out_14[1]), .Y0(out_14[0]), .Enable(Enable_2), .Reset(Reset_2));
  Register register_2 (
    .load(Load_3), .X3(out_14[3]), .X2(out_14[2]), .X1(out_14[1]), .X0(out_14[0]), .Y3(out_14[3]),
    .Y2(out_14[2]), .Y1(out_14[1]), .Y0(out_14[0]), .Enable(Enable_4), .Reset(Reset_4));
  Register register_3 (
    .load(Load_2), .X3(out_14[3]), .X2(out_14[2]), .X1(out_14[1]), .X0(out_14[0]), .Y3(out_14[3]),
    .Y2(out_14[2]), .Y1(out_14[1]), .Y0(out_14[0]), .Enable(Enable), .Reset(Reset));
  Register register_4 (
    .load(Load_4), .X3(out_14[3]), .X2(out_14[2]), .X1(out_14[1]), .X0(out_14[0]), .Y3(out_14[3]),
    .Y2(out_14[2]), .Y1(out_14[1]), .Y0(out_14[0]), .Enable(Enable_3), .Reset(Reset_3));

  // Notes on the sheet:
  //   Name: Md Saiful Islam
  //   Roll: 1607003
  //   RTL with 4 bit Register
  //   Output
endmodule

module Register (
  input  X1,
  input  X0,
  input  X3,
  input  X2,
  input  load,
  input  Reset,
  input  Enable,
  output Y3,
  output Y2,
  output Y1,
  output Y0
);

  wire clock_1_out, d_ff_1_q, d_ff_2_q, d_ff_3_q, d_ff_4_q, not_1_out, simple_ic_1_d, simple_ic_2_d,
       simple_ic_3_d, simple_ic_4_d;

  assign Y3 = Enable ? d_ff_1_q : 1'bz;  // Controlled_Buffer controlled_buffer_1
  not not_1 (not_1_out, load);
  D_Flip_Flop d_ff_1 (.clk(clock_1_out), .D(simple_ic_1_d), .Q(d_ff_1_q), .reset(Reset));  // open: Qn, preset, en
  simple_IC simple_ic_1 (.Load(load), .X(X3), .Load_prime(not_1_out), .Output(d_ff_1_q), .D(simple_ic_1_d));
  assign Y2 = Enable ? d_ff_2_q : 1'bz;  // Controlled_Buffer controlled_buffer_2
  simple_IC simple_ic_2 (.Load(load), .X(X2), .Load_prime(not_1_out), .Output(d_ff_2_q), .D(simple_ic_2_d));
  D_Flip_Flop d_ff_2 (.clk(clock_1_out), .D(simple_ic_2_d), .Q(d_ff_2_q), .reset(Reset));  // open: Qn, preset, en
  assign Y1 = Enable ? d_ff_3_q : 1'bz;  // Controlled_Buffer controlled_buffer_3
  D_Flip_Flop d_ff_3 (.clk(clock_1_out), .D(simple_ic_3_d), .Q(d_ff_3_q), .reset(Reset));  // open: Qn, preset, en
  simple_IC simple_ic_3 (.Load(load), .X(X1), .Load_prime(not_1_out), .Output(d_ff_3_q), .D(simple_ic_3_d));
  assign Y0 = Enable ? d_ff_4_q : 1'bz;  // Controlled_Buffer controlled_buffer_4
  D_Flip_Flop d_ff_4 (.clk(clock_1_out), .D(simple_ic_4_d), .Q(d_ff_4_q), .reset(Reset));  // open: Qn, preset, en
  simple_IC simple_ic_4 (.Load(load), .X(X0), .Load_prime(not_1_out), .Output(d_ff_4_q), .D(simple_ic_4_d));
  Clock clock_1 (.out(clock_1_out));

  // Notes on the sheet:
  //   Clock
  //   Name: Md Saiful Islam
  //   Roll: 1607003
  //   Clear
  //   Clock
  //   Clear
  //   4 bits register
  //   Clock
  //   Clear
  //   Clear
  //   Clock
endmodule

module simple_IC (
  input  Load,
  input  X,
  input  Load_prime,
  input  Output,
  output D
);

  wire and_1_out, and_2_out;

  and and_1 (and_1_out, Load, X);
  and and_2 (and_2_out, Load_prime, Output);
  or or_1 (D, and_1_out, and_2_out);

  // Notes on the sheet:
  //   Name: Md Saiful Islam
  //   Roll: 1607003
  //   a part of register circuit design
endmodule
