// Logisim project ALU.circ as structural Verilog: 3 circuits, main circuit main
module main (
  input  S1,
  input  S0,
  input  Cin,
  input  A0,
  input  B0,
  input  A1,
  input  B1,
  input  A2,
  input  B2,
  input  A3,
  input  B3,
  input  A4,
  input  B4,
  input  A5,
  input  B5,
  input  A6,
  input  B6,
  input  A7,
  input  B7,
  output F0,
  output F1,
  output F2,
  output F3,
  output F4,
  output F5,
  output F6,
  output F7,
  output C_out
);

  wire complement_1_b_or_b_com, complement_2_b_or_b_com, complement_3_b_or_b_com, complement_4_b_or_b_com,
       complement_5_b_or_b_com, complement_6_b_or_b_com, complement_7_b_or_b_com, complement_8_b_or_b_com,
       full_adder_1_c_out, full_adder_2_c_out, full_adder_3_c_out, full_adder_4_c_out, full_adder_5_c_out,
       full_adder_6_c_out, full_adder_7_c_out;

  Complement complement_1 (.B(B0), .S0(S0), .S1(S1), .B_Or_B_Com(complement_1_b_or_b_com));
  Complement complement_2 (.B(B1), .S0(S0), .S1(S1), .B_Or_B_Com(complement_2_b_or_b_com));
  Complement complement_3 (.B(B2), .S0(S0), .S1(S1), .B_Or_B_Com(complement_3_b_or_b_com));
  Complement complement_4 (.B(B3), .S0(S0), .S1(S1), .B_Or_B_Com(complement_4_b_or_b_com));
  Complement complement_5 (.B(B4), .S0(S0), .S1(S1), .B_Or_B_Com(complement_5_b_or_b_com));
  Complement complement_6 (.B(B5), .S0(S0), .S1(S1), .B_Or_B_Com(complement_6_b_or_b_com));
  Complement complement_7 (.B(B6), .S0(S0), .S1(S1), .B_Or_B_Com(complement_7_b_or_b_com));
  Complement complement_8 (.B(B7), .S0(S0), .S1(S1), .B_Or_B_Com(complement_8_b_or_b_com));
  Full_Adder full_adder_1 (.Cin(Cin), .A(A0), .B(complement_1_b_or_b_com), .Sum(F0), .C_Out(full_adder_1_c_out));
  Full_Adder full_adder_2 (
    .Cin(full_adder_1_c_out), .A(A1), .B(complement_2_b_or_b_com), .Sum(F1), .C_Out(full_adder_2_c_out));
  Full_Adder full_adder_3 (
    .Cin(full_adder_2_c_out), .A(A2), .B(complement_3_b_or_b_com), .Sum(F2), .C_Out(full_adder_3_c_out));
  Full_Adder full_adder_4 (
    .Cin(full_adder_3_c_out), .A(A3), .B(complement_4_b_or_b_com), .Sum(F3), .C_Out(full_adder_4_c_out));
  Full_Adder full_adder_5 (
    .Cin(full_adder_4_c_out), .A(A4), .B(complement_5_b_or_b_com), .Sum(F4), .C_Out(full_adder_5_c_out));
  Full_Adder full_adder_6 (
    .Cin(full_adder_5_c_out), .A(A5), .B(complement_6_b_or_b_com), .Sum(F5), .C_Out(full_adder_6_c_out));
  Full_Adder full_adder_7 (
    .Cin(full_adder_6_c_out), .A(A6), .B(complement_7_b_or_b_com), .Sum(F6), .C_Out(full_adder_7_c_out));
  Full_Adder full_adder_8 (.Cin(full_adder_7_c_out), .A(A7), .B(complement_8_b_or_b_com), .Sum(F7), .C_Out(C_out));

  // Notes on the sheet:
  //   Name: Md Saiful Islam
  //   Roll: 1607003
  //   Complementer
  //   Complementer
  //   Complementer
  //   Complementer
  //   Complementer
  //   Complementer
  //   Complementer
  //   Complementer
  //   Full Adder
  //   Full Adder
  //   Full Adder
  //   Full adder
  //   Full adder
  //   Full adder
  //   Full adder
  //   Full adder
  //   Name: Md Saiful Islam
  //   Roll: 1607003
  //   Let  A = 00000011
  //    B = 00000001
endmodule

module Complement (
  input  B,
  input  S0,
  input  S1,
  output B_Or_B_Com
);

  wire and_1_out, and_2_out, not_1_out;

  not not_1 (not_1_out, B);
  and and_1 (and_1_out, B, S0);
  and and_2 (and_2_out, not_1_out, S1);
  or or_1 (B_Or_B_Com, and_1_out, and_2_out);

  // Notes on the sheet:
  //   Name: Md Saiful Islam
  //   Roll: 1607003
endmodule

module Full_Adder (
  input  Cin,
  input  A,
  input  B,
  output Sum,
  output C_Out
);

  wire and_1_out, and_2_out, xor_1_out;

  xor xor_1 (xor_1_out, A, B);
  and and_1 (and_1_out, B, A);
  xor xor_2 (Sum, xor_1_out, Cin);
  and and_2 (and_2_out, Cin, xor_1_out);
  or or_1 (C_Out, and_2_out, and_1_out);

  // Notes on the sheet:
  //   Roll: 1607003
  //   Name: Md Saiful Islam
  //   A x-or B
  //   AB
  //   Cin ( A X-or B)
  //   = 
  //   Cin X-or ( A x-or B)
endmodule
