// Logisim project SAP-1 Computer_v2.circ as structural Verilog: 15 circuits, main circuit main
module main (
  output [3:0] High,
  output [3:0] Low,
  output [7:0] out_3
);

  wire Clock_out, control_sequencer_1_cp, control_sequencer_1_ea, control_sequencer_1_ep,
       control_sequencer_1_eu, control_sequencer_1_halt, control_sequencer_1_nce, control_sequencer_1_nei,
       control_sequencer_1_nla, control_sequencer_1_nlb, control_sequencer_1_nli, control_sequencer_1_nlm,
       control_sequencer_1_nlo, control_sequencer_1_su, controlled_buffer_1_out, not_1_out, not_2_out,
       not_3_out, Reset_out;
  wire [3:0] instruction_reg_1_instruction, mar_1_address_out;
  wire [7:0] accumulator_1_direct_output, b_reg_1_direct_output;

  RAM ram_1 ();  // open: Address, Input, Output, Store, nCE, CLK, CLR
  Multiplexer #(.width(4)) multiplexer_1 ();  // open: in0, in1, out, sel, en
  not not_1 (not_1_out, Reset_out);
  Program_Counter program_counter_1 (
    .Cp(control_sequencer_1_cp), .nCLR(not_1_out), .Ep(control_sequencer_1_ep), .out_6(Low),
    .Clk(controlled_buffer_1_out));  // open: out_5
  MAR mar_1 (
    .nLm(control_sequencer_1_nlm), .CLK(controlled_buffer_1_out), .CLR(Reset_out), .Address_In(Low),
    .Address_Out(mar_1_address_out));
  not not_2 (not_2_out, control_sequencer_1_nce);
  Instruction_Reg instruction_reg_1 (
    .nLi(control_sequencer_1_nli), .CLK(controlled_buffer_1_out), .CLR(Reset_out),
    .nEi(control_sequencer_1_nei), .Input({High, Low}), .Address(Low),
    .Instruction(instruction_reg_1_instruction));
  Control_Sequencer control_sequencer_1 (
    .Cp(control_sequencer_1_cp), .Ep(control_sequencer_1_ep), .nLm(control_sequencer_1_nlm),
    .nCE(control_sequencer_1_nce), .nLi(control_sequencer_1_nli), .nEi(control_sequencer_1_nei),
    .nLa(control_sequencer_1_nla), .Ea(control_sequencer_1_ea), .Su(control_sequencer_1_su),
    .Eu(control_sequencer_1_eu), .nLb(control_sequencer_1_nlb), .nLo(control_sequencer_1_nlo),
    .HALT(control_sequencer_1_halt), .CLK(controlled_buffer_1_out), .Reset(Reset_out),
    .Op_code(instruction_reg_1_instruction));
  RAM_part #(.addrWidth(4)) ram_2 (
    .addr(mar_1_address_out), .data({High, Low}), .ld(not_2_out));  // open: sel, clk, clr
  not not_3 (not_3_out, control_sequencer_1_halt);
  Clock Clock (.out(Clock_out));
  assign controlled_buffer_1_out = not_3_out ? Clock_out : 1'bz;  // Controlled_Buffer controlled_buffer_1
  Adder_Subtractor adder_subtractor_1 (
    .A(accumulator_1_direct_output), .A_2(b_reg_1_direct_output), .Eu(control_sequencer_1_eu),
    .Su(control_sequencer_1_su), .SUM_SUB({High, Low}));
  Button Reset (.out(Reset_out));
  Accumulator accumulator_1 (
    .CLK(controlled_buffer_1_out), .Ea(control_sequencer_1_ea), .Input({High, Low}), .\output ({High, Low}),
    .Direct_output(accumulator_1_direct_output), .nLa(control_sequencer_1_nla));  // open: CLR
  B_Reg b_reg_1 (
    .nLb(control_sequencer_1_nlb), .CLK(controlled_buffer_1_out), .CLR(Reset_out), .Input({High, Low}),
    .Direct_output(b_reg_1_direct_output));
  Out_Reg out_reg_1 (
    .nLo(control_sequencer_1_nlo), .CLK(controlled_buffer_1_out), .CLR(Reset_out), .Input({High, Low}),
    .Direct_output(out_3));
  Hex_Digit_Display hex_digit_display_1 (.value(out_3[3:0]));  // open: dp
  Hex_Digit_Display hex_digit_display_2 (.value(out_3[7:4]));  // open: dp

  // Notes on the sheet:
  //   Md. Repon Islam
  //   1607011
  //   Md. Saiful Islam
  //   1607003
endmodule

module Control_Sequencer (
  input  CLK,
  input  Reset,
  input  [3:0] Op_code,
  output Cp,
  output Ep,
  output nLm,
  output nCE,
  output nLi,
  output nEi,
  output nLa,
  output Ea,
  output Su,
  output Eu,
  output nLb,
  output nLo,
  output HALT
);

  wire and_1_out, and_2_out, and_3_out, and_4_out, and_5_out, and_6_out, and_7_out, and_8_out, and_9_out,
       and_10_out, and_11_out, and_13_out, and_15_out, and_16_out, and_17_out, and_18_out,
       cs_instruction_decoder_1_add, cs_instruction_decoder_1_lda, cs_instruction_decoder_1_out,
       cs_instruction_decoder_1_sub, Ring_Counter_t3, Ring_Counter_t4, Ring_Counter_t5, Ring_Counter_t6;

  CS_Instruction_Decoder cs_instruction_decoder_1 (
    .LDA(cs_instruction_decoder_1_lda), .ADD(cs_instruction_decoder_1_add),
    .SUB(cs_instruction_decoder_1_sub), .OUT(cs_instruction_decoder_1_out), .HLT(HALT), .I7(Op_code[3]),
    .I6(Op_code[2]), .I5(Op_code[1]), .I4(Op_code[0]));
  CS_Ring_Counter Ring_Counter (
    .RESET(Reset), .T6(Ring_Counter_t6), .T5(Ring_Counter_t5), .T4(Ring_Counter_t4), .T3(Ring_Counter_t3),
    .T2(Cp), .T1(Ep), .CLK(CLK));
  and and_1 (and_1_out, Ring_Counter_t4, cs_instruction_decoder_1_lda);
  and and_2 (and_2_out, Ring_Counter_t4, cs_instruction_decoder_1_sub);
  and and_3 (and_3_out, Ring_Counter_t4, cs_instruction_decoder_1_add);
  nor nor_1 (nLm, and_1_out, and_3_out, and_2_out, Ep);
  and and_4 (and_4_out, Ring_Counter_t5, cs_instruction_decoder_1_lda);
  and and_5 (and_5_out, Ring_Counter_t5, cs_instruction_decoder_1_sub);
  and and_6 (and_6_out, Ring_Counter_t5, cs_instruction_decoder_1_add);
  nor nor_2 (nCE, and_4_out, and_6_out, and_5_out, Ring_Counter_t3);
  and and_7 (and_7_out, Ring_Counter_t4, cs_instruction_decoder_1_lda);
  not not_1 (nLi, Ring_Counter_t3);
  and and_8 (and_8_out, Ring_Counter_t4, cs_instruction_decoder_1_sub);
  and and_9 (and_9_out, Ring_Counter_t4, cs_instruction_decoder_1_add);
  nor nor_3 (nEi, and_7_out, and_9_out, and_8_out);
  and and_10 (and_10_out, Ring_Counter_t5, cs_instruction_decoder_1_lda);
  and and_11 (and_11_out, Ring_Counter_t6, cs_instruction_decoder_1_add);
  nor nor_4 (nLa, and_10_out, and_11_out, and_13_out);
  and and_12 (Ea, Ring_Counter_t4, cs_instruction_decoder_1_out);
  and and_13 (and_13_out, Ring_Counter_t6, cs_instruction_decoder_1_sub);
  and and_14 (Su, Ring_Counter_t6, cs_instruction_decoder_1_sub);
  and and_15 (and_15_out, Ring_Counter_t6, cs_instruction_decoder_1_add);
  and and_16 (and_16_out, Ring_Counter_t6, cs_instruction_decoder_1_sub);
  or or_1 (Eu, and_15_out, and_16_out);
  and and_17 (and_17_out, Ring_Counter_t5, cs_instruction_decoder_1_sub);
  and and_18 (and_18_out, Ring_Counter_t5, cs_instruction_decoder_1_add);
  nor nor_5 (nLb, and_18_out, and_17_out);
  nand nand_1 (nLo, Ring_Counter_t4, cs_instruction_decoder_1_out);

  // Notes on the sheet:
  //   Md. Saiful Islam
  //   1607003
  //   Md. Repon Islam
  //   1607011
  //   Instruction Decoder
  //   T1 T2 T3 T4 T5 T6
endmodule

module CS_Instruction_Decoder (
  input  I7,
  input  I6,
  input  I5,
  input  I4,
  output LDA,
  output ADD,
  output SUB,
  output OUT,
  output HLT
);

  wire not_1_out, not_2_out, not_3_out, not_4_out;

  not not_1 (not_1_out, I7);
  not not_2 (not_2_out, I6);
  not not_3 (not_3_out, I5);
  not not_4 (not_4_out, I4);
  and and_1 (LDA, not_1_out, not_2_out, not_3_out, not_4_out);
  and and_2 (ADD, not_1_out, not_2_out, not_3_out, I4);
  and and_3 (SUB, not_1_out, not_2_out, I5, not_4_out);
  and and_4 (OUT, I7, I6, I5, not_4_out);
  and and_5 (HLT, I7, I6, I5, I4);

  // Notes on the sheet:
  //   Md Saiful Islam
  //   1607003
endmodule

module CS_Ring_Counter (
  input  CLK,
  input  RESET,
  output T6,
  output T5,
  output T4,
  output T3,
  output T2,
  output T1
);

  wire j_k_ff_1_qn, j_k_ff_2_qn, j_k_ff_3_qn, j_k_ff_4_qn, j_k_ff_5_qn, j_k_ff_6_q;

  J_K_Flip_Flop j_k_ff_1 (
    .J(T5), .clk(CLK), .K(j_k_ff_2_qn), .Q(T6), .Qn(j_k_ff_1_qn), .reset(RESET));  // open: preset, en
  J_K_Flip_Flop j_k_ff_2 (
    .J(T4), .clk(CLK), .K(j_k_ff_3_qn), .Q(T5), .Qn(j_k_ff_2_qn), .reset(RESET));  // open: preset, en
  J_K_Flip_Flop j_k_ff_3 (
    .J(T3), .clk(CLK), .K(j_k_ff_4_qn), .Q(T4), .Qn(j_k_ff_3_qn), .reset(RESET));  // open: preset, en
  J_K_Flip_Flop j_k_ff_4 (
    .J(T2), .clk(CLK), .K(j_k_ff_5_qn), .Q(T3), .Qn(j_k_ff_4_qn), .reset(RESET));  // open: preset, en
  J_K_Flip_Flop j_k_ff_5 (
    .J(T1), .clk(CLK), .K(j_k_ff_6_q), .Q(T2), .Qn(j_k_ff_5_qn), .reset(RESET));  // open: preset, en
  J_K_Flip_Flop j_k_ff_6 (
    .J(j_k_ff_1_qn), .clk(CLK), .K(T6), .Q(j_k_ff_6_q), .Qn(T1), .reset(RESET));  // open: preset, en

  // Notes on the sheet:
  //   1607003
  //   Md Saiful Islam
endmodule

module Register (
  input  [7:0] Input,
  input  LOAD,
  input  CLK,
  input  CLR,
  input  ENABLE,
  output [7:0] Direct_Output,
  output [7:0] Controlled_Output
);

  wire and_1_out, and_2_out, and_3_out, and_4_out, and_5_out, and_6_out, and_7_out, and_8_out, and_9_out,
       and_10_out, and_11_out, and_12_out, and_13_out, and_14_out, and_15_out, and_16_out, not_1_out,
       or_1_out, or_2_out, or_3_out, or_4_out, or_5_out, or_6_out, or_7_out, or_8_out;

  not not_1 (not_1_out, LOAD);
  and and_1 (and_1_out, not_1_out, Direct_Output[7]);
  and and_2 (and_2_out, Input[7], LOAD);
  or or_1 (or_1_out, and_2_out, and_1_out);
  and and_3 (and_3_out, Input[6], LOAD);
  D_Flip_Flop d_ff_1 (.clk(CLK), .D(or_1_out), .Q(Direct_Output[7]), .reset(CLR));  // open: Qn, preset, en
  and and_4 (and_4_out, not_1_out, Direct_Output[6]);
  or or_2 (or_2_out, and_3_out, and_4_out);
  D_Flip_Flop d_ff_2 (.clk(CLK), .D(or_2_out), .Q(Direct_Output[6]), .reset(CLR));  // open: Qn, preset, en
  and and_5 (and_5_out, not_1_out, Direct_Output[5]);
  and and_6 (and_6_out, Input[5], LOAD);
  or or_3 (or_3_out, and_6_out, and_5_out);
  D_Flip_Flop d_ff_3 (.clk(CLK), .D(or_3_out), .Q(Direct_Output[5]), .reset(CLR));  // open: Qn, preset, en
  and and_7 (and_7_out, Input[4], LOAD);
  and and_8 (and_8_out, not_1_out, Direct_Output[4]);
  or or_4 (or_4_out, and_7_out, and_8_out);
  D_Flip_Flop d_ff_4 (.clk(CLK), .D(or_4_out), .Q(Direct_Output[4]), .reset(CLR));  // open: Qn, preset, en
  and and_9 (and_9_out, Input[3], LOAD);
  or or_5 (or_5_out, and_9_out, and_10_out);
  and and_10 (and_10_out, not_1_out, Direct_Output[3]);
  D_Flip_Flop d_ff_5 (.clk(CLK), .D(or_5_out), .Q(Direct_Output[3]), .reset(CLR));  // open: Qn, preset, en
  assign Controlled_Output = ENABLE ? Direct_Output : 8'bz;  // Controlled_Buffer controlled_buffer_1
  and and_11 (and_11_out, not_1_out, Direct_Output[2]);
  and and_12 (and_12_out, Input[2], LOAD);
  or or_6 (or_6_out, and_12_out, and_11_out);
  and and_13 (and_13_out, Input[1], LOAD);
  D_Flip_Flop d_ff_6 (.clk(CLK), .D(or_6_out), .Q(Direct_Output[2]), .reset(CLR));  // open: Qn, preset, en
  and and_14 (and_14_out, not_1_out, Direct_Output[1]);
  or or_7 (or_7_out, and_13_out, and_14_out);
  D_Flip_Flop d_ff_7 (.clk(CLK), .D(or_7_out), .Q(Direct_Output[1]), .reset(CLR));  // open: Qn, preset, en
  and and_15 (and_15_out, Input[0], LOAD);
  or or_8 (or_8_out, and_15_out, and_16_out);
  and and_16 (and_16_out, not_1_out, Direct_Output[0]);
  D_Flip_Flop d_ff_8 (.clk(CLK), .D(or_8_out), .Q(Direct_Output[0]), .reset(CLR));  // open: Qn, preset, en

  // Notes on the sheet:
  //   1607011
  //   Md. Repon Islam
endmodule

// ACC
module Accumulator (
  input  nLa,
  input  [7:0] Input,
  input  CLK,
  input  CLR,
  input  Ea,
  output [7:0] \output ,
  output [7:0] Direct_output
);

  wire not_1_out;

  not not_1 (not_1_out, nLa);
  Register register_1 (
    .LOAD(not_1_out), .CLK(CLK), .CLR(CLR), .ENABLE(Ea), .Input(Input), .Direct_Output(Direct_output),
    .Controlled_Output(\output ));

  // Notes on the sheet:
  //   1607011
  //   Md. Repon Islam
endmodule

module B_Reg (
  input  nLb,
  input  [7:0] Input,
  input  CLK,
  input  CLR,
  output [7:0] Direct_output
);

  wire not_1_out;

  not not_1 (not_1_out, nLb);
  Register register_1 (
    .LOAD(not_1_out), .CLK(CLK), .CLR(CLR), .Input(Input), .Direct_Output(Direct_output));  // open: ENABLE, Controlled_Output

  // Notes on the sheet:
  //   1607011
  //   Md. Repon Islam
endmodule

// Out R
module Out_Reg (
  input  nLo,
  input  [7:0] Input,
  input  CLK,
  input  CLR,
  output [7:0] Direct_output
);

  wire not_1_out;

  not not_1 (not_1_out, nLo);
  Register register_1 (
    .LOAD(not_1_out), .CLK(CLK), .CLR(CLR), .Input(Input), .Direct_Output(Direct_output));  // open: ENABLE, Controlled_Output

  // Notes on the sheet:
  //   1607011
  //   Md. Repon Islam
endmodule

// IR
module Instruction_Reg (
  input  nLi,
  input  [7:0] Input,
  input  CLK,
  input  CLR,
  input  nEi,
  output [3:0] Address,
  output [3:0] Instruction
);

  wire not_1_out, not_2_out;
  wire [3:0] register_1_direct_output;
  wire [7:4] register_1_controlled_output;

  not not_1 (not_1_out, nLi);
  not not_2 (not_2_out, nEi);
  Register register_1 (
    .LOAD(not_1_out), .CLK(CLK), .CLR(CLR), .ENABLE(not_2_out), .Input(Input),
    .Direct_Output({Instruction, register_1_direct_output}),
    .Controlled_Output({register_1_controlled_output, Address}));

  // Notes on the sheet:
  //   1607011
  //   Md. Repon Islam
endmodule

module MAR (
  input  [3:0] Address_In,
  input  nLm,
  input  CLK,
  input  CLR,
  output [3:0] Address_Out
);

  wire not_1_out;
  wire [7:4] register_1_direct_output, undriven;

  not not_1 (not_1_out, nLm);
  Register register_1 (
    .LOAD(not_1_out), .CLK(CLK), .CLR(CLR), .Input({undriven, Address_In}),
    .Direct_Output({register_1_direct_output, Address_Out}));  // open: ENABLE, Controlled_Output

  // Notes on the sheet:
  //   1607011
  //   Md. Repon Islam
endmodule

module RAM (
  input  [3:0] Address,
  input  [7:0] Input,
  input  Store,
  input  nCE,
  input  CLK,
  input  CLR,
  output [7:0] Output
);

  wire and_1_out, and_2_out, and_3_out, and_4_out, and_5_out, and_6_out, and_7_out, and_8_out, and_9_out,
       and_10_out, and_11_out, and_12_out, and_13_out, and_14_out, and_15_out, and_16_out, not_1_out,
       not_2_out, not_3_out, not_4_out;
  wire [2:2] not_5_out;

  not not_1 (not_1_out, Address[2]);
  not not_2 (not_2_out, Address[3]);
  not not_3 (not_3_out, Address[1]);
  not not_4 (not_4_out, Address[0]);
  and and_1 (and_1_out, not_4_out, not_3_out, not_1_out, not_2_out);
  and and_2 (and_2_out, Address[0], not_3_out, not_1_out, not_2_out);
  and and_3 (and_3_out, not_4_out, Address[1], not_1_out, not_2_out);
  and and_4 (and_4_out, Address[0], Address[1], not_1_out, not_2_out);
  and and_5 (and_5_out, not_4_out, not_3_out, Address[2], not_2_out);
  and and_6 (and_6_out, Address[0], not_3_out, Address[2], not_2_out);
  and and_7 (and_7_out, not_4_out, Address[1], Address[2], not_2_out);
  and and_8 (and_8_out, Address[0], Address[1], Address[2], not_2_out);
  and and_9 (and_9_out, not_4_out, not_3_out, not_1_out, Address[3]);
  and and_10 (and_10_out, Address[0], not_3_out, not_1_out, Address[3]);
  and and_11 (and_11_out, not_4_out, Address[1], not_1_out, Address[3]);
  and and_12 (and_12_out, Address[0], Address[1], not_1_out, Address[3]);
  and and_13 (and_13_out, not_4_out, not_3_out, Address[2], Address[3]);
  and and_14 (and_14_out, Address[0], not_3_out, Address[2], Address[3]);
  and and_15 (and_15_out, not_4_out, Address[1], Address[2], Address[3]);
  and and_16 (and_16_out, Address[0], Address[1], Address[2], Address[3]);
  BC_Reg bc_reg_1 (
    .Select(and_1_out), .Input(Input), .Output(Output), .Str_Ld__CLK__CLR({Store, not_5_out[2], CLK, CLR}));
  BC_Reg bc_reg_2 (
    .Select(and_2_out), .Input(Input), .Output(Output), .Str_Ld__CLK__CLR({Store, not_5_out[2], CLK, CLR}));
  BC_Reg bc_reg_3 (
    .Select(and_3_out), .Input(Input), .Output(Output), .Str_Ld__CLK__CLR({Store, not_5_out[2], CLK, CLR}));
  BC_Reg bc_reg_4 (
    .Select(and_4_out), .Input(Input), .Output(Output), .Str_Ld__CLK__CLR({Store, not_5_out[2], CLK, CLR}));
  BC_Reg bc_reg_5 (
    .Select(and_5_out), .Input(Input), .Output(Output), .Str_Ld__CLK__CLR({Store, not_5_out[2], CLK, CLR}));
  BC_Reg bc_reg_6 (
    .Select(and_6_out), .Input(Input), .Output(Output), .Str_Ld__CLK__CLR({Store, not_5_out[2], CLK, CLR}));
  BC_Reg bc_reg_7 (
    .Select(and_7_out), .Input(Input), .Output(Output), .Str_Ld__CLK__CLR({Store, not_5_out[2], CLK, CLR}));
  BC_Reg bc_reg_8 (
    .Select(and_8_out), .Input(Input), .Output(Output), .Str_Ld__CLK__CLR({Store, not_5_out[2], CLK, CLR}));
  BC_Reg bc_reg_9 (
    .Select(and_9_out), .Input(Input), .Output(Output), .Str_Ld__CLK__CLR({Store, not_5_out[2], CLK, CLR}));
  BC_Reg bc_reg_10 (
    .Select(and_10_out), .Input(Input), .Output(Output), .Str_Ld__CLK__CLR({Store, not_5_out[2], CLK, CLR}));
  BC_Reg bc_reg_11 (
    .Select(and_11_out), .Input(Input), .Output(Output), .Str_Ld__CLK__CLR({Store, not_5_out[2], CLK, CLR}));
  BC_Reg bc_reg_12 (
    .Select(and_12_out), .Input(Input), .Output(Output), .Str_Ld__CLK__CLR({Store, not_5_out[2], CLK, CLR}));
  BC_Reg bc_reg_13 (
    .Select(and_13_out), .Input(Input), .Output(Output), .Str_Ld__CLK__CLR({Store, not_5_out[2], CLK, CLR}));
  BC_Reg bc_reg_14 (
    .Select(and_14_out), .Input(Input), .Output(Output), .Str_Ld__CLK__CLR({Store, not_5_out[2], CLK, CLR}));
  BC_Reg bc_reg_15 (
    .Select(and_15_out), .Input(Input), .Output(Output), .Str_Ld__CLK__CLR({Store, not_5_out[2], CLK, CLR}));
  BC_Reg bc_reg_16 (
    .Select(and_16_out), .Input(Input), .Output(Output), .Str_Ld__CLK__CLR({Store, not_5_out[2], CLK, CLR}));
  not not_5 (not_5_out[2], nCE);

  // Notes on the sheet:
  //   1607011
  //   Md. Repon Islam
endmodule

// BC
module BC_Reg (
  input  Select,
  input  [7:0] Input,
  input  [3:0] Str_Ld__CLK__CLR,
  output [7:0] Output
);

  wire and_1_out, and_2_out;

  and and_1 (and_1_out, Select, Str_Ld__CLK__CLR[3]);
  and and_2 (and_2_out, Select, Str_Ld__CLK__CLR[2]);
  Register register_1 (
    .LOAD(and_1_out), .CLK(Str_Ld__CLK__CLR[1]), .CLR(Str_Ld__CLK__CLR[0]), .ENABLE(and_2_out),
    .Input(Input), .Controlled_Output(Output));  // open: Direct_Output

  // Notes on the sheet:
  //   Str
endmodule

// FA
module Full_Adder (
  input  Cin,
  input  A,
  input  B,
  output Sum,
  output C_Out
);

  wire and_1_out, and_2_out, xor_1_out;

  xor xor_1 (xor_1_out, A, B);
  and and_1 (and_1_out, B, A);
  xor xor_2 (Sum, xor_1_out, Cin);
  and and_2 (and_2_out, Cin, xor_1_out);
  or or_1 (C_Out, and_2_out, and_1_out);

  // Notes on the sheet:
  //   Roll: 1607003
  //   Name: Md Saiful Islam
  //   A x-or B
  //   AB
  //   Cin ( A X-or B)
  //   = 
  //   Cin X-or ( A x-or B)
endmodule

// Add/Sub
module Adder_Subtractor (
  input  [7:0] A,
  input  [7:0] A_2,
  input  Su,
  input  Eu,
  output [7:0] SUM_SUB
);

  wire full_adder_2_c_out, full_adder_3_c_out, full_adder_4_c_out, full_adder_5_c_out, full_adder_6_c_out,
       full_adder_7_c_out, full_adder_8_c_out, xor_1_out, xor_2_out, xor_3_out, xor_4_out, xor_5_out,
       xor_6_out, xor_7_out, xor_8_out;
  wire [7:0] full_adder_8_sum;

  Full_Adder full_adder_1 (
    .Cin(full_adder_2_c_out), .A(A[7]), .B(xor_1_out), .Sum(full_adder_8_sum[7]));  // open: C_Out
  xor xor_1 (xor_1_out, A_2[7], Su);
  Full_Adder full_adder_2 (
    .Cin(full_adder_3_c_out), .A(A[6]), .B(xor_2_out), .Sum(full_adder_8_sum[6]), .C_Out(full_adder_2_c_out));
  xor xor_2 (xor_2_out, A_2[6], Su);
  Full_Adder full_adder_3 (
    .Cin(full_adder_4_c_out), .A(A[5]), .B(xor_3_out), .Sum(full_adder_8_sum[5]), .C_Out(full_adder_3_c_out));
  xor xor_3 (xor_3_out, A_2[5], Su);
  Full_Adder full_adder_4 (
    .Cin(full_adder_5_c_out), .A(A[4]), .B(xor_4_out), .Sum(full_adder_8_sum[4]), .C_Out(full_adder_4_c_out));
  assign SUM_SUB = Eu ? full_adder_8_sum : 8'bz;  // Controlled_Buffer controlled_buffer_1
  xor xor_4 (xor_4_out, A_2[4], Su);
  Full_Adder full_adder_5 (
    .Cin(full_adder_6_c_out), .A(A[3]), .B(xor_5_out), .Sum(full_adder_8_sum[3]), .C_Out(full_adder_5_c_out));
  xor xor_5 (xor_5_out, A_2[3], Su);
  Full_Adder full_adder_6 (
    .Cin(full_adder_7_c_out), .A(A[2]), .B(xor_6_out), .Sum(full_adder_8_sum[2]), .C_Out(full_adder_6_c_out));
  xor xor_6 (xor_6_out, A_2[2], Su);
  Full_Adder full_adder_7 (
    .Cin(full_adder_8_c_out), .A(A[1]), .B(xor_7_out), .Sum(full_adder_8_sum[1]), .C_Out(full_adder_7_c_out));
  xor xor_7 (xor_7_out, A_2[1], Su);
  Full_Adder full_adder_8 (.Cin(Su), .A(A[0]), .B(xor_8_out), .Sum(full_adder_8_sum[0]), .C_Out(full_adder_8_c_out));
  xor xor_8 (xor_8_out, A_2[0], Su);

  // Notes on the sheet:
  //   1607003
  //   Md Saiful Islam
endmodule

// PC
module Program_Counter (
  input  Cp,
  input  Clk,
  input  nCLR,
  input  Ep,
  output [3:0] out_5,
  output [3:0] out_6
);

  wire not_1_out, not_2_out, not_3_out, not_4_out, not_5_out;

  not not_1 (not_1_out, Clk);
  not not_2 (not_2_out, nCLR);
  J_K_Flip_Flop j_k_ff_1 (.J(Cp), .clk(not_1_out), .K(Cp), .Q(out_5[0]), .reset(not_2_out));  // open: Qn, preset, en
  not not_3 (not_3_out, out_5[0]);
  J_K_Flip_Flop j_k_ff_2 (.J(Cp), .clk(not_3_out), .K(Cp), .Q(out_5[1]), .reset(not_2_out));  // open: Qn, preset, en
  not not_4 (not_4_out, out_5[1]);
  J_K_Flip_Flop j_k_ff_3 (.J(Cp), .clk(not_4_out), .K(Cp), .Q(out_5[2]), .reset(not_2_out));  // open: Qn, preset, en
  assign out_6 = Ep ? out_5 : 4'bz;  // Controlled_Buffer controlled_buffer_1
  not not_5 (not_5_out, out_5[2]);
  J_K_Flip_Flop j_k_ff_4 (.J(Cp), .clk(not_5_out), .K(Cp), .Q(out_5[3]), .reset(not_2_out));  // open: Qn, preset, en

  // Notes on the sheet:
  //   1607003
  //   Md Saiful Islam
endmodule
